// Logisim project ULA_4BITS_OFC.circ as structural Verilog: 1 circuit, main circuit main
module main (
  input  ADD_SUB,
  input  A3,
  input  A2,
  input  A1,
  input  A0,
  input  B3,
  input  B2,
  input  B1,
  input  B0,
  input  [1:0] in_10,
  input  XOR_NOT,
  output Y3,
  output Y1,
  output Y2,
  output Y0,
  output Overflow
);

  wire adder_1_cout, adder_1_out, adder_2_cout, adder_2_out, adder_3_cout, adder_3_out, adder_4_out,
       and_1_out, and_2_out, and_3_out, and_4_out, or_1_out, or_2_out, or_3_out, or_4_out, or_5_out,
       or_6_out, or_7_out, or_8_out, xor_1_out, xor_2_out, xor_3_out, xor_4_out, xor_5_out, xor_6_out,
       xor_7_out, xor_8_out;

  xor xor_1 (xor_1_out, B0, ADD_SUB);
  xor xor_2 (xor_2_out, B1, ADD_SUB);
  xor xor_3 (xor_3_out, B2, ADD_SUB);
  xor xor_4 (xor_4_out, B3, ADD_SUB);
  or or_1 (or_1_out, B3, XOR_NOT);
  or or_2 (or_2_out, B2, XOR_NOT);
  or or_3 (or_3_out, B1, XOR_NOT);
  or or_4 (or_4_out, B0, XOR_NOT);
  Adder #(.width(1)) adder_1 (.a(A0), .b(xor_1_out), .out(adder_1_out), .cin(ADD_SUB), .cout(adder_1_cout));
  Adder #(.width(1)) adder_2 (.a(A1), .b(xor_2_out), .out(adder_2_out), .cin(adder_1_cout), .cout(adder_2_cout));
  Adder #(.width(1)) adder_3 (.a(A2), .b(xor_3_out), .out(adder_3_out), .cin(adder_2_cout), .cout(adder_3_cout));
  Adder #(.width(1)) adder_4 (.a(A3), .b(xor_4_out), .out(adder_4_out), .cin(adder_3_cout), .cout(Overflow));
  and and_1 (and_1_out, A3, B3);
  and and_2 (and_2_out, A2, B2);
  and and_3 (and_3_out, A1, B1);
  and and_4 (and_4_out, A0, B0);
  or or_5 (or_5_out, A3, B3);
  or or_6 (or_6_out, A2, B2);
  or or_7 (or_7_out, A1, B1);
  or or_8 (or_8_out, A0, B0);
  xor xor_5 (xor_5_out, A3, or_1_out);
  xor xor_6 (xor_6_out, A2, or_2_out);
  xor xor_7 (xor_7_out, A1, or_3_out);
  xor xor_8 (xor_8_out, A0, or_4_out);
  Multiplexer #(.select(2), .enable("false")) multiplexer_1 (
    .in0(adder_4_out), .in1(and_1_out), .in2(or_5_out), .in3(xor_5_out), .out(Y3), .sel(in_10));
  Multiplexer #(.select(2), .enable("false")) multiplexer_2 (
    .in0(adder_3_out), .in1(and_2_out), .in2(or_6_out), .in3(xor_6_out), .out(Y1), .sel(in_10));
  Multiplexer #(.select(2), .enable("false")) multiplexer_3 (
    .in0(adder_2_out), .in1(and_3_out), .in2(or_7_out), .in3(xor_7_out), .out(Y2), .sel(in_10));
  Multiplexer #(.select(2), .enable("false")) multiplexer_4 (
    .in0(adder_1_out), .in1(and_4_out), .in2(or_8_out), .in3(xor_8_out), .out(Y0), .sel(in_10));

  // Notes on the sheet:
  //   OPERAÇÕES
  //   SOMADOR/SUBTRADOR
  //   AND
  //   OR
  //   XOR/NOT
  //   00
  //   01
  //   10
  //   11
endmodule
